# Fritzing sketch PulseSensorFeedback (saved by Fritzing 0.7.6b)
breadboards: 1

parts:
  Arduino1 = Arduino
  LED1 = LED - 5mm [color="Red (633nm)" package="5 mm [THT]"]  # not connected
  R1 = Rotary Potentiometer (Small) [maximum_resistance=100kΩ]

nets:
  N1: Arduino1.GND, R1.leg2
  N2: Arduino1.A0, R1.leg1

notes:
  Connect Blue line to Analog0
